# Fritzing sketch nRF24 Raspberry Pi adapter (saved by Fritzing 0.8.7b)

parts:
  NRF24L1 = NRF24L01
  Raspberry_Pi_B_rev1 = Raspberry Pi B rev2

nets:
  VCC: NRF24L1.VCC, Raspberry_Pi_B_rev1.3V3
  GND: NRF24L1.GND, Raspberry_Pi_B_rev1.GND

custom parts:
  NRF24L01: NRF24L01 module
