# Fritzing sketch nRF24-Arduino-adapter (saved by Fritzing 0.8.7b)

parts:
  NRF24L1 = NRF24L01
  Part1 = Arduino Uno (Rev3) - ICSP
  C1 = Electrolytic Capacitor [capacitance=1µF package="100 mil [THT, electrolytic]"]

nets:
  VCC: NRF24L1.VCC, Part1.3V3, C1.+
  N1: NRF24L1.CSN, Part1.D10_PWM/SS
  N2: NRF24L1.MOSI, Part1.D11_PWM/MOSI
  GND: NRF24L1.GND, Part1.GND, C1.-
  N3: NRF24L1.CE, Part1.D9_PWM
  N4: NRF24L1.SCK, Part1.D13/SCK
  N5: NRF24L1.MISO, Part1.D12/MISO

custom parts:
  NRF24L01: NRF24L01 module
